# Fritzing sketch Kontrolni uređaj (saved by Fritzing 0.9.3b)
breadboards: 1

parts:
  R1 = Resistor [tolerance=±5% resistance=220 package=THT]
  R2 = Resistor [tolerance=±5% resistance=220 package=THT]
  R3 = Resistor [tolerance=±5% resistance=220 package=THT]
  Pico = Raspberry Pi Pico
  R4 = Resistor [tolerance=±5% resistance=220 package=THT]
  Prevoius_mode_button = Pushbutton [package="[THT]"]
  Increase_button = Pushbutton [package="[THT]"]
  LCD_display = LCD1602-I2C
  Decrease_button = Pushbutton [package="[THT]"]
  Next_mode_button = Pushbutton [package="[THT]"]

nets:
  N1: R1.Pin_0, R2.Pin_0, R3.Pin_0, R4.Pin_0, LCD_display.GND
  N2: R1.Pin_1, Pico.pin_21, Next_mode_button.Pin_1, Next_mode_button.Pin_2
  N3: R2.Pin_1, Pico.pin_25, Prevoius_mode_button.Pin_1, Prevoius_mode_button.Pin_2
  N4: R3.Pin_1, Pico.pin_24, Decrease_button.Pin_1, Decrease_button.Pin_2
  N5: Pico.pin_22, R4.Pin_1, Increase_button.Pin_1, Increase_button.Pin_2
  N6: Pico.pin_31, LCD_display.SDA
  N7: Pico.pin_32, LCD_display.SCL
  N8: Pico.pin_36, Prevoius_mode_button.Pin_3, Prevoius_mode_button.Pin_4, Increase_button.Pin_3, Increase_button.Pin_4, LCD_display.VCC, Decrease_button.Pin_3, Decrease_button.Pin_4, Next_mode_button.Pin_3, Next_mode_button.Pin_4

custom parts:
  Raspberry Pi Pico: Raspberry Pi Pico. Based around the RP2040 microcontroller the Pico is a low cost microcontroller device bringing Raspberry Pi quality, cost, and easy of use to the microcontroller space. Jan 2021, Split part in to two versions: tht (this one) and SMD. This one will drill holes for a .1 in header in pcb to allow plugging in the module as well as providing pads to solder the module to the top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
  LCD1602-I2C: A standard character display, usually with 2x16 characters. Comes in many colors with LCM1602 IIC attached.
