# Fritzing sketch Terenski_uređaj (saved by Fritzing 0.9.3b)
breadboards: 1

parts:
  T1 = LM35 Temperature Sensor [package="TO92 [THT]"]
  J1 = Piezo Speaker
  LED4 = LED - 5mm [color="Red (633nm)" package="5 mm [THT]"]
  LED5 = LED - 5mm [color="Red (633nm)" package="5 mm [THT]"]
  LED7 = LED - 5mm [color="Red (633nm)" package="5 mm [THT]"]
  LED3 = LED - 5mm [color="Red (633nm)" package="5 mm [THT]"]
  LED1 = LED - 5mm [color="Red (633nm)" package="5 mm [THT]"]
  LED6 = LED - 5mm [color="Red (633nm)" package="5 mm [THT]"]
  LED2 = LED - 5mm [color="Red (633nm)" package="5 mm [THT]"]
  R1 = Resistor [tolerance=±5% resistance=220 package="0603 [SMD]"]
  R2 = Resistor [tolerance=±5% resistance=220 package="0603 [SMD]"]
  R3 = Resistor [tolerance=±5% resistance=220 package="0603 [SMD]"]
  R4 = Resistor [tolerance=±5% resistance=220 package="0603 [SMD]"]
  R5 = Resistor [tolerance=±5% resistance=220 package="0603 [SMD]"]
  R6 = Resistor [tolerance=±5% resistance=220 package="0603 [SMD]"]
  R7 = Resistor [tolerance=±5% resistance=220 package="0603 [SMD]"]
  Pico = Raspberry Pi Pico
  BAT1 = BC9VPC [package=bc9vpc]
  R9 = Resistor [tolerance=±5% resistance=220 package="0603 [SMD]"]
  Alarm_off_button = Pushbutton [package="[THT]"]
  Q2 = npn-Powertransistor [package="TO220 [THT]"]
  D1 = Rectifier Diode [part_number=1N4001 package="300 mil [THT]"]
  M1 = DC Motor

nets:
  N1: T1.+Vs, Pico.pin_36, R9.Pin_1, Alarm_off_button.Pin_1, Alarm_off_button.Pin_2
  N2: T1.Vout, Pico.pin_34
  N3: T1.GND, J1.pin1, R1.Pin_0, R2.Pin_0, R3.Pin_0, R4.Pin_0, R5.Pin_0, R6.Pin_0, R7.Pin_0, Pico.pin_3, Pico.pin_28, Pico.pin_33, Pico.pin_38, BAT1.V-, Q2.emitter
  N4: J1.pin2, Pico.pin_32
  N5: LED4.cathode, R4.Pin_1
  N6: LED4.anode, Pico.pin_10
  N7: LED5.cathode, R5.Pin_1
  N8: LED5.anode, Pico.pin_11
  N9: LED7.cathode, R7.Pin_1
  N10: LED7.anode, Pico.pin_14
  N11: LED3.cathode, R3.Pin_1
  N12: LED3.anode, Pico.pin_9
  N13: LED1.cathode, R1.Pin_1
  N14: LED1.anode, Pico.pin_6
  N15: LED6.cathode, R6.Pin_1
  N16: LED6.anode, Pico.pin_12
  N17: LED2.cathode, R2.Pin_1
  N18: LED2.anode, Pico.pin_7
  N19: Pico.pin_1, R9.Pin_0, Alarm_off_button.Pin_3, Alarm_off_button.Pin_4
  N20: Pico.pin_29, Q2.base
  N21: BAT1.V+, D1.cathode, M1.pin_1
  N22: Q2.collector, D1.anode, M1.pin_2

custom parts:
  Raspberry Pi Pico: Raspberry Pi Pico. Based around the RP2040 microcontroller the Pico is a low cost microcontroller device bringing Raspberry Pi quality, cost, and easy of use to the microcontroller space. Jan 2021, Split part in to two versions: tht (this one) and SMD. This one will drill holes for a .1 in header in pcb to allow plugging in the module as well as providing pads to solder the module to the top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
